// Digital circuit memory_fpga.dig as structural Verilog
module memory_fpga (
  input  clk,
  output [5:0] led
);

  wire u_clkdiv_clk_out;
  wire [31:0] u_counter_count, u_memory_o_mem_data;

  clkdiv #(.applicationType("IVERILOG"), .CodeFile("clk_div.v")) u_clkdiv (.clk(clk), .clk_out(u_clkdiv_clk_out));
  counter #(.applicationType("IVERILOG"), .CodeFile("counter.v")) u_counter (
    .clk(u_clkdiv_clk_out), .resetn(1'b1), .count(u_counter_count));
  memory #(.applicationType("IVERILOG"), .CodeFile("memory.v")) u_memory (
    .clk(clk), .mem_addr(u_counter_count), .i_mem_data({32{1'b0}}), .mem_rw(1'b1),
    .o_mem_data(u_memory_o_mem_data));
  assign led = ~u_memory_o_mem_data[5:0];  // Not not_1, 6 bits wide

  // Notes on the sheet:
  //   clk: Hz: 10
endmodule
