// Digital circuit soc.dig as structural Verilog
module soc (
  input  clk,
  output [31:0] x10
);

  wire [13:0] u_cpu_pc_2;
  wire [31:0] rom_d, u_cpu_pc;

  BlockRAMDualPort blockramdualport_1 ();  // open: A, Din, str, C, D
  ROM #(.AddrBits(14), .Bits(32)) rom (.A(u_cpu_pc_2), .sel(1'b1), .D(rom_d));
  cpu #(.applicationType("IVERILOG"), .CodeFile("cpu.v")) u_cpu (
    .instr(rom_d), .resetn(1'b1), .clk(clk), .PC({u_cpu_pc[31:16], u_cpu_pc_2, u_cpu_pc[1:0]}), .x10(x10));

  // Notes on the sheet:
  //   clk: Hz: 10
  //   contents of rom (hex, n*v repeats v):
  //   513,a00593,b50663,150513,ff9ff06f,100073
endmodule
