// Digital circuit soc_fpga.dig as structural Verilog
module soc_fpga (
  input  btn1,
  input  clk,
  output [5:0] led
);

  wire u_clkdiv_clk_out;
  wire [13:0] u_cpu_pc_2;
  wire [31:0] rom_d, u_cpu_pc, u_cpu_x1;

  ROM #(.AddrBits(14), .Bits(32)) rom (.A(u_cpu_pc_2), .sel(1'b1), .D(rom_d));
  clkdiv #(.applicationType("IVERILOG"), .CodeFile("clk_div.v")) u_clkdiv (.clk(clk), .clk_out(u_clkdiv_clk_out));
  cpu #(.applicationType("IVERILOG"), .CodeFile("cpu.v")) u_cpu (
    .instr(rom_d), .resetn(btn1), .clk(u_clkdiv_clk_out), .PC({u_cpu_pc[31:16], u_cpu_pc_2, u_cpu_pc[1:0]}),
    .x1(u_cpu_x1));
  assign led = ~u_cpu_x1[5:0];  // Not not_1, 6 bits wide

  // Notes on the sheet:
  //   clk: Hz: 10
  //   contents of rom (hex, n*v repeats v):
  //   b3,3f00113,108093,fe209ee3,b3,ff5ff06f
endmodule
